// Logisim project Lab9.circ as structural Verilog: 4 circuits, main circuit datapath
module datapath (
  input  [4:0] in_1,
  output [2:0] out_2,
  output [2:0] out_3
);

  wire clock_1_out, clock_2_out;
  wire [2:0] multiplexer_1_out, multiplexer_2_out, shifter_1_out;

  Register #(.width(3)) HL (.D(multiplexer_2_out), .en(in_1[4]), .clk(clock_1_out), .Q(out_2));  // open: clr
  Clock clock_1 (.out(clock_1_out));
  Register #(.width(3)) FL (.D(multiplexer_2_out), .en(in_1[3]), .clk(clock_2_out), .Q(out_3));  // open: clr
  Clock clock_2 (.out(clock_2_out));
  Multiplexer #(.width(3)) multiplexer_1 (.in0(out_2), .in1(out_3), .out(multiplexer_1_out), .sel(in_1[2]));
  Multiplexer #(.select(2), .width(3)) multiplexer_2 (
    .in0(3'b001), .in1(3'b100), .in2(shifter_1_out), .in3(shifter_1_out), .out(multiplexer_2_out),
    .sel(in_1[1:0]));
  Shifter #(.shift("rl"), .width(3)) shifter_1 (.in(multiplexer_1_out), .\dist (2'b01), .out(shifter_1_out));
endmodule

module controlunit (
  input  RESET,
  input  CLK_In,
  input  CAR_DETECT,
  output [4:0] out_4
);

  wire and_1_out, comparator_1_eq, comparator_2_eq, not_1_out, not_2_out, or_1_out;
  wire [5:0] counter_1_q;

  not not_1 (not_1_out, comparator_1_eq);
  Comparator #(.width(6)) comparator_1 (.a(counter_1_q), .b({6{1'b0}}), .eq(comparator_1_eq));  // open: gt, lt
  not not_2 (not_2_out, comparator_2_eq);
  Comparator #(.width(6)) comparator_2 (.a(counter_1_q), .b(6'b000001), .eq(comparator_2_eq));  // open: gt, lt
  and and_1 (and_1_out, RESET, not_1_out);
  or or_1 (or_1_out, CAR_DETECT, not_2_out);
  Counter #(.max('h2d), .width(6)) counter_1 (
    .load(and_1_out), .up(1'b1), .count(or_1_out), .clk(CLK_In), .D({6{1'b0}}), .Q(counter_1_q));  // open: clr, carry
  ROM #(.addrWidth(6), .dataWidth(5)) rom_1 (.addr(counter_1_q), .data(out_4));

  // Notes on the sheet:
  //   contents of rom_1 (hex, n*v repeats v):
  //   10 9 12 0 0 0 12 e 16*0 e 0 0 0 e 12
endmodule

module Sanitizer (
  input  [2:0] HL_in,
  input  [2:0] FL_in,
  output out_3,
  output out_4,
  output out_5,
  output out_6,
  output out_7,
  output out_8
);

  wire and_1_out, and_5_out, and_7_out;

  and and_1 (and_1_out, ~HL_in[0], FL_in[0]);  // AND_Gate
  and and_2 (out_4, ~HL_in[2], HL_in[1]);  // AND_Gate
  and and_3 (out_5, ~HL_in[2], ~HL_in[1], HL_in[0]);  // AND_Gate
  and and_4 (out_8, ~FL_in[2], ~FL_in[1], and_1_out);  // AND_Gate
  and and_5 (and_5_out, ~out_4, ~out_5);  // AND_Gate
  and and_6 (out_7, ~FL_in[2], FL_in[1]);  // AND_Gate
  or or_1 (out_3, HL_in[2], and_5_out);
  or or_2 (out_6, FL_in[2], and_7_out);
  and and_7 (and_7_out, ~out_7, ~out_8);  // AND_Gate
endmodule

module Traffic (
  input  in_1,
  input  in_2
);

  wire clock_1_out, sanitizer_1_out_3, sanitizer_1_out_4, sanitizer_1_out_5, sanitizer_1_out_6,
       sanitizer_1_out_7, sanitizer_1_out_8;
  wire [2:0] datapath_1_out_2, datapath_1_out_3;
  wire [4:0] controlunit_1_out_4;

  Clock clock_1 (.out(clock_1_out));
  controlunit controlunit_1 (.RESET(in_1), .CLK_In(clock_1_out), .CAR_DETECT(in_2), .out_4(controlunit_1_out_4));
  datapath datapath_1 (.in_1(controlunit_1_out_4), .out_2(datapath_1_out_2), .out_3(datapath_1_out_3));
  LED led_1 (.in(sanitizer_1_out_3));
  Sanitizer sanitizer_1 (
    .HL_in(datapath_1_out_2), .FL_in(datapath_1_out_3), .out_3(sanitizer_1_out_3), .out_4(sanitizer_1_out_4),
    .out_5(sanitizer_1_out_5), .out_6(sanitizer_1_out_6), .out_7(sanitizer_1_out_7), .out_8(sanitizer_1_out_8));
  LED led_2 (.in(sanitizer_1_out_4));
  LED led_3 (.in(sanitizer_1_out_5));
  LED led_4 (.in(sanitizer_1_out_6));
  LED led_5 (.in(sanitizer_1_out_7));
  LED led_6 (.in(sanitizer_1_out_8));
endmodule
